# Fritzing sketch counter (saved by Fritzing 0.9.3b)
breadboards: 1

parts:
  Part1 = Arduino Uno (Rev3)
  S1 = Pushbutton [package="[THT]"]
  R1 = Resistor [tolerance=±5% resistance=10k package=THT]
  LED1 = LED - 5mm [color="Red (633nm)" package="5 mm [THT]"]
  R2 = Resistor [tolerance=±5% resistance=220 package=THT]
  R3 = Resistor [tolerance=±5% resistance=10k package=THT]
  R4 = Photocell (LDR) [package=THT]

nets:
  N1: Part1.GND, Part1.D4, R1.Pin_0, LED1.cathode, R3.Pin_1
  N2: Part1.D2, R3.Pin_0, R4.pin_0
  N3: Part1.5V, S1.Pin_1, S1.Pin_2, R2.Pin_0, R4.pin_1
  N4: S1.Pin_3, S1.Pin_4, R1.Pin_1
  N5: LED1.anode, R2.Pin_1
